# Fritzing sketch batterie-controleur-diagrame-cablage-v2 (saved by Fritzing 0.9.3b)
circuit board: 9cm x 7cm
perfboards: 1

parts:
  Composant2 = Arduino Nano (Rev3.0)
  PNP3 = npn-Powertransistor [package="TO220 [THT]"]
  PNP4 = npn-Powertransistor [package="TO220 [THT]"]
  PNP2 = npn-Powertransistor [package="TO220 [THT]"]
  Alim_connectors_-_0_1 = Camdenboss CTB0158-3 [part_number=CTB0158-3 package=THT]
  J1 = Camdenboss CTB0158-5 [part_number=CTB0158-5 package=THT]
  NPN1 = pnp-Powertransistor [part_number=PNP1 package="TO220 [THT]"]
  NPN3 = pnp-Powertransistor [package="TO220 [THT]"]
  NPN = pnp-Powertransistor [package="TO220 [THT]"]
  NPN4 = pnp-Powertransistor [package="TO220 [THT]"]
  1K = Resistor [tolerance=±5% resistance=1k package=THT]
  1K1 = Resistor [tolerance=±5% resistance=1k package=THT]
  1K2 = Resistor [tolerance=±5% resistance=1k package=THT]
  1K3 = Resistor [tolerance=±5% resistance=1k package=THT]
  1K4 = Resistor [tolerance=±5% resistance=1k package=THT]
  1K5 = Resistor [tolerance=±5% resistance=1k package=THT]
  1K6 = Resistor [tolerance=±5% resistance=1k package=THT]
  1K7 = Resistor [tolerance=±5% resistance=1k package=THT]
  PNP1 = npn-Powertransistor [package="TO220 [THT]"]
  J2 = Camdenboss CTB0158-5 [part_number=CTB0158-5 package=THT]  # not connected
  JP2 = FTDI_BASIC [package=ftdi_basic]
  10K_-_1 = Resistor [tolerance=±5% resistance=10k package=THT]
  10K_-_2 = Resistor [tolerance=±5% resistance=10k package=THT]
  5k_-_1 = Resistor [tolerance=±5% resistance=5k package=THT]
  5k_-_2 = Resistor [tolerance=±5% resistance=5k package=THT]
  10k1 = Resistor [tolerance=±5% resistance=10k package=THT]
  10k2 = Resistor [tolerance=±5% resistance=10k package=THT]
  10k3 = Resistor [tolerance=±5% resistance=10k package=THT]
  10k4 = Resistor [tolerance=±5% resistance=10k package=THT]
  JP3 = FTDI_BASIC [package=ftdi_basic]
  Buzzer = Piezo Speaker
  JS1 = Generic Jumper Shunt

nets:
  N1: Composant2.GND, JP2.2
  N2: Composant2.D2, JP3.4
  N3: Composant2.D3, JP3.3
  N4: Composant2.D7, JS1.pin1
  N5: Composant2.5V, JP2.1
  N6: Composant2.A7, 10K_-_1.Pin_0, 5k_-_1.Pin_1
  N7: Composant2.A6, 10K_-_2.Pin_1, 5k_-_2.Pin_1
  N8: Composant2.A3, 1K6.Pin_0
  N9: Composant2.A2, 1K4.Pin_0
  N10: Composant2.A1, 1K5.Pin_0
  N11: Composant2.A0, 1K7.Pin_0
  N12: PNP3.base, 1K2.Pin_1
  N13: PNP3.collector, PNP4.collector, PNP2.collector, Alim_connectors_-_0_1.pin3, PNP1.collector, 10k1.Pin_1, 10k2.Pin_1, 10k3.Pin_1, 10k4.Pin_1
  N14: PNP3.emitter, J1.pin4
  N15: PNP4.base, 1K3.Pin_1
  N16: PNP4.emitter, J1.pin5
  N17: PNP2.base, 1K1.Pin_1
  N18: PNP2.emitter, J1.pin2
  N19: Alim_connectors_-_0_1.pin2, NPN1.emitter, NPN3.emitter, NPN.emitter, NPN4.emitter, 5k_-_1.Pin_0, 5k_-_2.Pin_0
  N20: J1.pin1, PNP1.emitter
  N21: NPN1.base, 1K5.Pin_1
  N22: NPN1.collector, 1K2.Pin_0
  N23: NPN3.base, 1K6.Pin_1
  N24: NPN3.collector, 1K.Pin_0
  N25: NPN.base, 1K7.Pin_1
  N26: NPN.collector, 1K3.Pin_0
  N27: NPN4.base, 1K4.Pin_1
  N28: NPN4.collector, 1K1.Pin_0
  N29: 1K.Pin_1, PNP1.base
  N30: JP2.3, 10K_-_1.Pin_1
  N31: JP2.4, 10K_-_2.Pin_0
  N32: Buzzer.pin2, JS1.pin2
