# Fritzing sketch batterie-controleur-diagrame-cablage-v3 (saved by Fritzing 0.9.3b)
circuit board: 9cm x 7cm
perfboards: 1

parts:
  R1-1K = Resistor [tolerance=±5% resistance=1k package=THT]
  1K1 = Resistor [tolerance=±5% resistance=1k package=THT]
  1K2 = Resistor [tolerance=±5% resistance=1k package=THT]
  1K3 = Resistor [tolerance=±5% resistance=1k package=THT]
  1K4 = Resistor [tolerance=±5% resistance=1k package=THT]
  R2-1K = Resistor [tolerance=±5% resistance=1k package=THT]
  R3-1K = Resistor [tolerance=±5% resistance=1k package=THT]
  R4-1K = Resistor [tolerance=±5% resistance=1k package=THT]
  R3-10k = Resistor [tolerance=±5% resistance=10k package=THT]
  R4-10k = Resistor [tolerance=±5% resistance=10k package=THT]
  R2-10k = Resistor [tolerance=±5% resistance=10k package=THT]
  R1-10K = Resistor [tolerance=±5% resistance=10k package=THT]
  Buzzer = Piezo Speaker
  JS1 = Generic Jumper Shunt
  D2 = Schottky Diode [part_number=1N5817 package="300 mil [THT]"]
  D4 = Schottky Diode [part_number=1N5817 package="300 mil [THT]"]
  D1 = Schottky Diode [part_number=1N5817 package="300 mil [THT]"]
  Composant2 = Arduino Nano (Rev3.0)
  Load_Relay = Camdenboss CTB0158-2 [part_number=CTB0158-2 package=THT]
  Charge_Relay = Camdenboss CTB0158-2 [part_number=CTB0158-2 package=THT]
  -_/_GND_/_12V = Camdenboss CTB0158-2 [part_number=CTB0158-2 package=THT]
  D3 = Schottky Diode [part_number=1N5817 package="300 mil [THT]"]
  NPN4 = npn-Powertransistor [package="TO220 [THT]"]
  NPN1 = npn-Powertransistor [package="TO220 [THT]"]
  NPN2 = npn-Powertransistor [package="TO220 [THT]"]
  PNP3 = pnp-Powertransistor [package="TO220 [THT]"]
  PNP4 = pnp-Powertransistor [package="TO220 [THT]"]
  PNP2 = pnp-Powertransistor [package="TO220 [THT]"]
  PNP1 = pnp-Powertransistor [package="TO220 [THT]"]
  NPN3 = npn-Powertransistor [package="TO220 [THT]"]
  J3 = Camdenboss CTB0158-10 [part_number=CTB0158-10 package=THT]
  0_1uF = Electrolytic Capacitor [capacitance=100nF package="100 mil [THT, electrolytic]"]
  GND_/_5V = Camdenboss CTB0158-2 [part_number=CTB0158-2 package=THT]
  0_1uF1 = Electrolytic Capacitor [capacitance=100nF package="100 mil [THT, electrolytic]"]
  Relay_states_(GND) = Camdenboss CTB0158-2 [part_number=CTB0158-2 package=THT]
  R1-10K1 = Resistor [tolerance=±5% resistance=10k package=THT]
  R1-10K2 = Resistor [tolerance=±5% resistance=10k package=THT]

nets:
  N1: R1-1K.Pin_0, R1-10K.Pin_0, NPN1.collector
  N2: R1-1K.Pin_1, PNP4.base
  N3: 1K1.Pin_0, Composant2.A0
  N4: 1K1.Pin_1, NPN4.base
  N5: 1K2.Pin_0, Composant2.A1
  N6: 1K2.Pin_1, NPN3.base
  N7: 1K3.Pin_0, Composant2.A2
  N8: 1K3.Pin_1, NPN2.base
  N9: 1K4.Pin_0, Composant2.A3
  N10: 1K4.Pin_1, NPN1.base
  N11: R2-1K.Pin_0, R2-10k.Pin_0, NPN2.collector
  N12: R2-1K.Pin_1, PNP3.base
  N13: R3-1K.Pin_0, R3-10k.Pin_0, NPN3.collector
  N14: R3-1K.Pin_1, PNP2.base
  N15: R4-1K.Pin_0, R4-10k.Pin_0, NPN4.collector
  N16: R4-1K.Pin_1, PNP1.base
  N17: R3-10k.Pin_1, R4-10k.Pin_1, R2-10k.Pin_1, R1-10K.Pin_1, -_/_GND_/_12V.pin2, PNP3.emitter, PNP4.emitter, PNP2.emitter, PNP1.emitter
  N18: Buzzer.pin1, Composant2.GND, J3.pin2, 0_1uF.-
  N19: Buzzer.pin2, JS1.pin2
  N20: JS1.pin1, Composant2.D7
  N21: D2.cathode, Charge_Relay.pin1, PNP2.collector
  N22: D2.anode, D4.anode, D1.anode, -_/_GND_/_12V.pin1, D3.anode, NPN4.emitter, NPN1.emitter, NPN2.emitter, NPN3.emitter
  N23: D4.cathode, Load_Relay.pin1, PNP4.collector
  N24: D1.cathode, Charge_Relay.pin2, PNP1.collector
  N25: Composant2.5V, J3.pin1, 0_1uF.+, GND_/_5V.pin2, 0_1uF1.+, R1-10K1.Pin_0, R1-10K2.Pin_0
  N26: Composant2.A5, J3.pin3
  N27: Composant2.A4, J3.pin4
  N28: Load_Relay.pin2, D3.cathode, PNP3.collector
  N29: GND_/_5V.pin1, 0_1uF1.-
  N30: Relay_states_(GND).pin1, R1-10K1.Pin_1
  N31: Relay_states_(GND).pin2, R1-10K2.Pin_1
