# Fritzing sketch batterie-controleur-diagrame-cablage (saved by Fritzing 0.9.3b)
circuit board: 8.46667cm x 5.64444cm
perfboards: 1

parts:
  Composant2 = Arduino Nano (Rev3.0)
  Q1 = npn-Powertransistor [package="TO220 [THT]"]
  Q4 = npn-Powertransistor [package="TO220 [THT]"]
  Q5 = npn-Powertransistor [package="TO220 [THT]"]
  Q6 = npn-Powertransistor [package="TO220 [THT]"]
  J2 = Camdenboss CTB0158-3 [part_number=CTB0158-3 package=THT]
  JP1 = Header 8 [package=1x08_smd]  # not connected
  D1 = Diode [package=diode-1n4001]
  J1 = Camdenboss CTB0158-5 [part_number=CTB0158-5 package=THT]
  R6 = Resistor [tolerance=±5% resistance=10k package=THT]
  R7 = Resistor [tolerance=±5% resistance=10k package=THT]
  R8 = Resistor [tolerance=±5% resistance=10k package=THT]
  R9 = Resistor [tolerance=±5% resistance=10k package=THT]

nets:
  N1: Composant2.D9, R6.Pin_1
  N2: Composant2.D10, R7.Pin_1
  N3: Composant2.D11/MOSI, R8.Pin_1
  N4: Composant2.D12/MISO, R9.Pin_1
  N5: Q1.base, J1.pin5
  N6: Q1.collector, Q4.collector, Q5.collector, Q6.collector, J2.pin1, D1.A
  N7: Q4.base, J1.pin2
  N8: Q4.emitter, R8.Pin_0
  N9: Q5.base, J1.pin1
  N10: Q6.base, J1.pin4
  N11: J2.pin2, D1.C
